# Fritzing sketch schematic (saved by Fritzing 0.9.3b)
breadboards: 1

parts:
  S2 = Round Pushbutton
  U1 = LIPO-1000mAh [package=lipo-1000]
  LED1 = LED - 3mm [color="Red (633nm)" package="3 mm [THT]"]
  R1 = Resistor [tolerance=±5% resistance=220 package="2010 [SMD]"]
  Part1 = Thumb Joystick
  U2 = CAPSENSE_PAD [package=capsense_pad]  # not connected
  R2 = PHOTOCELL [package=photocell]
  R3 = Resistor [tolerance=±5% resistance=220 package=THT]

nets:
  N1: S2.leg0, U1.+
  N2: LED1.cathode, Part1.VCC, R2.P$1
  N3: LED1.anode, R1.Pin_0
  N4: R1.Pin_1, Part1.GND, R3.Pin_1
  N5: R2.P$2, R3.Pin_0

notes:
  DIY Aluminum foil sensor
