# Fritzing sketch schematic (saved by Fritzing 0.9.3b)
breadboards: 1

parts:
  BREAKOUT1 = ULN2003A breakout board
  J1 = Basic Servo
  S1 = Square Pushbutton

nets:
  N1: BREAKOUT1.0V, J1.gnd, S1.leg1
  +5V: BREAKOUT1.+5V, J1.vcc

custom parts:
  ULN2003A breakout board: ULN2003A 7-way Darlington Transistor Driver on breakoutboard
