# Fritzing sketch schematic (saved by Fritzing 0.9.3b)
breadboards: 4

parts:
  R1 = PHOTOCELL [package=photocell]
  R2 = PHOTOCELL [package=photocell]
  R3 = PHOTOCELL [package=photocell]
  R4 = PHOTOCELL [package=photocell]
  R5 = PHOTOCELL [package=photocell]
  R6 = PHOTOCELL [package=photocell]
  R7 = PHOTOCELL [package=photocell]
  R8 = PHOTOCELL [package=photocell]
  R9 = PHOTOCELL [package=photocell]
  R10 = PHOTOCELL [package=photocell]
  R11 = PHOTOCELL [package=photocell]
  R12 = PHOTOCELL [package=photocell]
  R14 = PHOTOCELL [package=photocell]
  R15 = Resistor [tolerance=±5% resistance=220 package="0402 [SMD]"]
  R16 = Resistor [tolerance=±5% resistance=220 package="0402 [SMD]"]
  R17 = Resistor [tolerance=±5% resistance=220 package="0402 [SMD]"]
  R18 = Resistor [tolerance=±5% resistance=220 package="0402 [SMD]"]
  R19 = Resistor [tolerance=±5% resistance=220 package="0402 [SMD]"]
  R20 = Resistor [tolerance=±5% resistance=220 package="0402 [SMD]"]
  R21 = Resistor [tolerance=±5% resistance=220 package="0402 [SMD]"]
  R22 = Resistor [tolerance=±5% resistance=220 package="0402 [SMD]"]
  R23 = Resistor [tolerance=±5% resistance=220 package="0402 [SMD]"]
  R24 = Resistor [tolerance=±5% resistance=220 package="0402 [SMD]"]
  R25 = Resistor [tolerance=±5% resistance=220 package="0402 [SMD]"]
  R26 = Resistor [tolerance=±5% resistance=220 package="0402 [SMD]"]
  R27 = Resistor [tolerance=±5% resistance=220 package="0402 [SMD]"]
  LED1 = smd LED [color="Red (633nm)" package="0603 [SMD]"]
  LED2 = smd LED [color="Red (633nm)" package="0603 [SMD]"]
  LED3 = smd LED [color="Red (633nm)" package="0603 [SMD]"]
  LED4 = smd LED [color="Red (633nm)" package="0603 [SMD]"]
  LED5 = smd LED [color="Red (633nm)" package="0603 [SMD]"]
  LED6 = smd LED [color="Red (633nm)" package="0603 [SMD]"]
  LED7 = smd LED [color="Red (633nm)" package="0603 [SMD]"]
  LED8 = smd LED [color="Red (633nm)" package="0603 [SMD]"]
  LED9 = smd LED [color="Red (633nm)" package="0603 [SMD]"]
  LED10 = smd LED [color="Red (633nm)" package="0603 [SMD]"]
  LED11 = smd LED [color="Red (633nm)" package="0603 [SMD]"]
  LED12 = smd LED [color="Red (633nm)" package="0603 [SMD]"]
  LED13 = smd LED [color="Red (633nm)" package="0603 [SMD]"]
  Part1 = OLED Monochrome 128x64 1.3 inch [part_number=938]  # not connected
  RE1 = Rotary Encoder [package=THT]
  S1 = Square Pushbutton  # not connected

nets:
  N1: R1.P$1, R2.P$1, R3.P$1, R4.P$1, R5.P$1, R6.P$1, R7.P$1, R8.P$1, R9.P$1, R10.P$1, R11.P$1, R12.P$1, R14.P$1
  N2: R1.P$2, R15.Pin_0
  N3: R2.P$2, R16.Pin_0
  N4: R3.P$2, R17.Pin_0
  N5: R4.P$2, R18.Pin_0
  N6: R5.P$2, R19.Pin_0
  N7: R6.P$2, R20.Pin_0
  N8: R7.P$2, R21.Pin_0
  N9: R8.P$2, R22.Pin_0
  N10: R9.P$2, R23.Pin_0
  N11: R10.P$2, R24.Pin_0
  N12: R11.P$2, R26.Pin_0
  N13: R12.P$2, R27.Pin_0
  N14: R14.P$2, R25.Pin_0
  N15: R15.Pin_1, R16.Pin_1, R17.Pin_1, R18.Pin_1, R19.Pin_1, R20.Pin_1, R21.Pin_1, R22.Pin_1, R23.Pin_1, R24.Pin_1, R25.Pin_1, R26.Pin_1, R27.Pin_1, LED1.cathode, LED2.cathode, LED3.cathode, LED4.cathode, LED5.cathode, LED6.cathode, LED7.cathode, LED8.cathode, LED9.cathode, LED10.cathode, LED11.cathode, LED12.cathode, LED13.cathode, RE1.EncoderPinC

custom parts:
  OLED Monochrome 128x64 1.3 inch: These displays are small, only about 1.3" diagonal, but very readable due to the high contrast of an OLED display. This display is made of 128x64 individual white OLED pixels, each one is turned on or off by the controller chip. Because the display makes its own light, no backlight is required. This reduces the power required to run the OLED and is why the display has such high contrast; we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
