# Fritzing sketch schematic (saved by Fritzing 0.9.3b)
breadboards: 1

parts:
  Part1 = Arduino Uno (Rev3) - ICSP
  BATT1 = 4xAA Switchable Battery Pack w/Bare Wire
  RE1 = Rotary Encoder [package=THT]
  RE2 = Rotary Encoder [package=THT]
  RE3 = Rotary Encoder [package=THT]
  RE4 = Rotary Encoder [package=THT]
  J1 = Basic Servo
  J2 = Basic Servo
  J3 = Basic Servo
  J4 = Basic Servo
  HC-SR04_Sensor_1 = HC-SR04 Ultrasonic Distance Sensor

nets:
  N1: Part1.A0, HC-SR04_Sensor_1.TRIG
  N2: Part1.A1, HC-SR04_Sensor_1.ECHO
  N3: Part1.ICSP_MISO, Part1.D12/MISO, J4.pulse
  N4: Part1.D8, RE4.EncoderPinB
  N5: Part1.D9_PWM, RE4.EncoderPinA
  N6: Part1.D10_PWM/SS, J2.pulse
  N7: Part1.D11_PWM/MOSI, J1.pulse
  N8: Part1.D13/SCK, J3.pulse
  N9: Part1.D2, RE1.EncoderPinB
  N10: Part1.D3_PWM, RE1.EncoderPinA
  N11: Part1.D4, RE2.EncoderPinB
  N12: Part1.D5_PWM, RE2.EncoderPinA
  N13: Part1.D6_PWM, RE3.EncoderPinB
  N14: Part1.D7, RE3.EncoderPinA
  5V: Part1.5V, HC-SR04_Sensor_1.VCC
  GND: Part1.GND, RE1.EncoderPinC, RE2.EncoderPinC, RE3.EncoderPinC, RE4.EncoderPinC, HC-SR04_Sensor_1.GND
  VCC: BATT1.POS, J1.vcc, J2.vcc, J3.vcc, J4.vcc
  GND_2: BATT1.NEG, J1.gnd, J2.gnd, J3.gnd, J4.gnd

custom parts:
  4xAA Switchable Battery Pack w/Bare Wire: 4xAA Switchable Battery Pack with Bare Wire connection
