# Fritzing sketch part1_diagram (saved by Fritzing 0.9.3b)
breadboards: 1

parts:
  Part1 = Arduino Uno (Rev3) - ICSP
  S1 = Pushbutton [package="[THT]"]
  R2 = Resistor [tolerance=±5% resistance=220 package=THT]

nets:
  N1: Part1.GND, S1.Pin_1, S1.Pin_2
  N2: Part1.D2, S1.Pin_3, S1.Pin_4, R2.Pin_0
  N3: Part1.5V, R2.Pin_1
