# Fritzing sketch part3_diagram (saved by Fritzing 0.9.3b)
breadboards: 1

parts:
  Part1 = Arduino Uno (Rev3) - ICSP
  U1 = 74HC595 [package="DIP16 [THT]"]
  U2 = 74HC595 [package="DIP16 [THT]"]
  Dot_Matrix1 = LED Dot Matrix 18mm (0.7 INCH)
  R1 = Resistor [tolerance=±5% resistance=220 package="2010 [SMD]"]
  R2 = Resistor [tolerance=±5% resistance=220 package="2010 [SMD]"]
  R3 = Resistor [tolerance=±5% resistance=220 package="2010 [SMD]"]
  R4 = Resistor [tolerance=±5% resistance=220 package="2010 [SMD]"]
  R5 = Resistor [tolerance=±5% resistance=220 package="2010 [SMD]"]
  S1 = Pushbutton [package="[THT]"]

nets:
  VCC: Part1.5V, U1.MR, U1.VCC, U2.MR, U2.VCC
  N1: Part1.D2, S1.Pin_1, S1.Pin_2
  N2: Part1.D5_PWM, U2.ST_CP
  GND: Part1.GND, U1.GND, U1.OE, U2.GND, U2.OE, S1.Pin_3, S1.Pin_4
  N3: U1.Q1, Dot_Matrix1.Row_2
  N4: U1.Q2, Dot_Matrix1.Row_3
  N5: U1.Q4, Dot_Matrix1.Row_5
  N6: U1.Q5, Dot_Matrix1.Row_6
  N7: U1.Q6, Dot_Matrix1.Row_7
  N8: U1.Q0, Dot_Matrix1.Row_1
  N9: U2.Q2, R3.Pin_0
  N10: U2.Q3, R2.Pin_0
  N11: U2.Q4, R1.Pin_0
  N12: U2.Q0, R5.Pin_0
  N13: Dot_Matrix1.Column_1, R5.Pin_1
  N14: Dot_Matrix1.Column_2, R4.Pin_1
  N15: Dot_Matrix1.Column_4, R2.Pin_1
  N16: Dot_Matrix1.Column_5, R1.Pin_1
  N17: Dot_Matrix1.Column_3, R3.Pin_1
