# Fritzing sketch sketch_part1 (saved by Fritzing 0.9.3b)
breadboards: 1

parts:
  Part1 = Arduino Uno (Rev3) - ICSP
  R1 = Photocell (LDR) [package=THT]
  R2 = Resistor [tolerance=±5% resistance=10k package="2512 [SMD]"]
  LED1 = RGB LED (com. anode, rbg) [package="5 mm [THT]"]
  R3 = Resistor [tolerance=±5% resistance=220 package="2512 [SMD]"]

nets:
  N1: Part1.A0, R1.pin_1, R2.Pin_0
  N2: Part1.5V, R1.pin_0
  N3: Part1.GND, R2.Pin_1, R3.Pin_1
  N4: Part1.D11_PWM/MOSI, LED1.common_anode
  N5: LED1.blue_cathode, R3.Pin_0
