# Fritzing sketch sketch_part2 (saved by Fritzing 0.9.3b)
breadboards: 1

parts:
  Part1 = Arduino Uno (Rev3) - ICSP
  R1 = Photocell (LDR) [package=THT]
  R2 = Resistor [tolerance=±5% resistance=10k package="2010 [SMD]"]
  HC-SR04_Sensor_1 = HC-SR04 Ultrasonic Distance Sensor
  LED1 = RGB LED (com. anode, rbg) [package="5 mm [THT]"]
  R3 = Resistor [tolerance=±5% resistance=220 package=THT]
  R4 = Resistor [tolerance=±5% resistance=220 package=THT]
  R5 = Resistor [tolerance=±5% resistance=220 package=THT]

nets:
  N1: Part1.A0, R1.pin_0, R2.Pin_1
  5V: Part1.5V, R1.pin_1, HC-SR04_Sensor_1.VCC
  N2: Part1.D8, HC-SR04_Sensor_1.GND
  N3: Part1.D11_PWM/MOSI, LED1.common_anode
  N4: Part1.GND, R2.Pin_0, HC-SR04_Sensor_1.ECHO
  N5: Part1.D3_PWM, R5.Pin_1
  N6: Part1.D4, R4.Pin_1
  N7: Part1.D5_PWM, R3.Pin_1
  N8: Part1.D7, HC-SR04_Sensor_1.TRIG
  N9: LED1.red_cathode, R5.Pin_0
  N10: LED1.blue_cathode, R4.Pin_0
  N11: LED1.green_cathode, R3.Pin_0
