# Fritzing sketch sketch_part3 (saved by Fritzing 0.9.3b)
breadboards: 1

parts:
  Part1 = Arduino Uno (Rev3) - ICSP
  RE1 = Rotary Encoder [package=THT]
  OLED1 = 128x64 Monochrom OLED Display with SPI Control

nets:
  5V: Part1.5V, OLED1.Vin
  N1: Part1.D8, OLED1.Reset
  N2: Part1.D9_PWM, OLED1.SA0/DC
  N3: Part1.D10_PWM/SS, OLED1.CS
  N4: Part1.D2, RE1.EncoderPinA
  N5: Part1.D3_PWM, RE1.EncoderPinB
  N6: Part1.D6_PWM, OLED1.Clock
  N7: Part1.D7, OLED1.Data
  GND: Part1.GND, RE1.EncoderPinC, OLED1.GND
